# Fritzing sketch DIAGRAM (saved by Fritzing 0.9.3b)
breadboards: 1

parts:
  Part1 = Arduino Uno (Rev3) - ICSP
  A1 = DFR0379
  RELAY = 1 chan 3v relay module
  JACK1 = 2.1mm Barrel Jack with Terminal Block
  POWER = Bill acceptor TB74-U
  Part3 = Coin Acceptor - 6-Coin version
  Part4 = Thermal Printer

nets:
  N1: Part1.D10_PWM/SS, Part4.RXD
  N2: Part1.D11_PWM/MOSI, Part4.TXD
  GND: Part1.GND, A1.Pin_3, A1.Pin_4, A1.Pin_5, A1.Pin_6, RELAY.pin_3, JACK1.NEG, POWER.Pin_13, Part3.GND, Part4.GND#0
  N3: Part1.D2, POWER.Pin_12
  N4: Part1.D3_PWM, Part3.C5
  N5: Part1.D7, RELAY.pin_2
  N6: Part1.5V, RELAY.pin_1
  N7: A1.Pin_1, A1.Pin_2, RELAY.pin_8, POWER.Pin_11, Part3.12V
  N8: A1.Pin_7, A1.Pin_8, Part4.VH
  N9: RELAY.pin_7, JACK1.POS

notes:
  COIN ACCEPTOR: NEVERMIND OTHER WIRINGS, FOCUS ONLY SA GND, 12V, COIN
  NOTE: C5 AS COIN
  NOTE: POWER PIN (4 PIN)
  -- NO PIN,
  -- BLACK AS GND,
  -- CYAN AS SIGNAL,
  -- RED AS VCC
  12V ADAPTER CONNECT TO THIS FEMALE BARREL JACK
  THERMAL PRINTER VCC CONNECTED TO OUT- STEP DOWN CONVERTER
  THERMAL PRINTER VCC CONNECTED TO OUT+ STEP DOWN CONVERTER
  NOTE: THERMAL PRINTER PIN. (GND, RX, TX, DTR, VH)
  CONNECT THE GND TO STEPDOWN OUT-
  CONNECT THE VH TO STEPDOWN OUT+
  CONNECT THE RX TO DIGITAL PIN 10 OF ARDUINO
  CONNECT THE TX TO DIGITAL PIN 11 OF ARDUINO
  LEAVE THE DTR NO PIN

custom parts:
  DFR0379: 20W Adjustable DC-DC Buck Converter with Digital Display.
  1 chan 3v relay module: Single 3V relay isolated drive control module High level drive board.
  Bill acceptor TB74-U: The TB-Series is the latest generation of banknote reader designed exclusively by TOPVME with the highest safety and acceptance rate have over 96%.
  Coin Acceptor - 6-Coin version: 12V coin acceptor that can handle up to 6 different denominations. Output is either pulse width, serial, or single pin per coin value.
